# Fritzing sketch ProyectoIOT (saved by Fritzing 0.9.3b)
breadboards: 1

parts:
  U1 = ESP32S-HiLetgo [part_number=ESP32S-HiLetgo]
  PIR1 = PIR sensor
  DHT1 = DHT11 Humitidy and Temperature Sensor
  J3 = Basic Servo
  LED1 = smd LED [color="Red (633nm)" package="0603 [SMD]"]
  Componente4 = Adafruit MiCS-5524 Gas Sensor [part_number="Adafruit #3199"]
  J4 = Piezo Speaker

nets:
  N1: U1.GPIO27, J4.pin2
  N2: U1.GPIO14, J3.pulse
  N3: U1.GPIO12, PIR1.SIG
  GND: U1.GND, J3.gnd, LED1.cathode, Componente4.GND, J4.pin1
  N4: U1.GPIO13, DHT1.DATA
  VIN: U1.VIN, J3.vcc, Componente4.5.0V
  N5: U1.GPIO2, LED1.anode
  N6: U1.GPIO4, Componente4.AOUT, Componente4.ENABLE

custom parts:
  ESP32S-HiLetgo: HiLetgo ESP-WROOM-32 ESP32 ESP-32S Development Board 2.4GHz Dual-Mode WiFi + Bluetooth Dual Cores Microcontroller The ESP32 integrated with Antenna switches, RF Balun, power amplifiers, low-noise amplifiers, filters, and management modules, and the entire solution occupies the least area of PCB. 2.4 GHz Wi-Fi plus Bluetooth dual-mode chip, with TSMC Ultra-low power consumption 40nm technology,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
  DHT11 Humitidy and Temperature Sensor: DHT11 Humidity and Temperature Sensor
  Adafruit MiCS-5524 Gas Sensor: Give your next sensor project a nose for gasses with the Adafruit MiCS-5524 Gas Sensor Breakout. This breakout makes it easy to use this nice sensor from SGX Sensortech. The MiCS-5524 is a robust MEMS sensor for indoor carbon monoxide and natural gas leakage detection, it's suitable also for indoor air quality monitoring; breath checker and early fire detection. Please note: This sensor is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
